// Logisim project ALU.circ as structural Verilog: 2 circuits, main circuit ALU
module FullAdder_1b (
  input  A,
  input  B,
  input  C_in,
  output Sum,
  output C_out
);

  wire and_1_out, and_2_out, xor_1_out;

  and and_1 (and_1_out, A, B);
  xor xor_1 (xor_1_out, A, B);
  and and_2 (and_2_out, xor_1_out, C_in);
  xor xor_2 (Sum, xor_1_out, C_in);
  or or_1 (C_out, and_2_out, and_1_out);
endmodule

module ALU (
  input  [7:0] A,
  input  Subtraction,
  input  [7:0] B,
  output [7:0] res,
  output Overflow
);

  wire Bit_toplama_2_c_out, Bit_toplama_3_c_out, Bit_toplama_4_c_out, Bit_toplama_5_c_out,
       Bit_toplama_6_c_out, Bit_toplama_7_c_out, Bit_toplama_8_c_out, xor_1_out, xor_2_out, xor_3_out,
       xor_4_out, xor_5_out, xor_6_out, xor_7_out, xor_8_out;

  FullAdder_1b Bit_toplama_1 (.A(A[7]), .B(xor_1_out), .C_in(Bit_toplama_2_c_out), .Sum(res[7]), .C_out(Overflow));
  xor xor_1 (xor_1_out, B[7], Subtraction);
  xor xor_2 (xor_2_out, B[6], Subtraction);
  xor xor_3 (xor_3_out, B[5], Subtraction);
  xor xor_4 (xor_4_out, B[4], Subtraction);
  xor xor_5 (xor_5_out, B[3], Subtraction);
  xor xor_6 (xor_6_out, B[2], Subtraction);
  xor xor_7 (xor_7_out, B[1], Subtraction);
  xor xor_8 (xor_8_out, B[0], Subtraction);
  FullAdder_1b Bit_toplama_2 (
    .A(A[6]), .B(xor_2_out), .C_in(Bit_toplama_3_c_out), .Sum(res[6]), .C_out(Bit_toplama_2_c_out));
  FullAdder_1b Bit_toplama_3 (
    .A(A[5]), .B(xor_3_out), .C_in(Bit_toplama_4_c_out), .Sum(res[5]), .C_out(Bit_toplama_3_c_out));
  FullAdder_1b Bit_toplama_4 (
    .A(A[4]), .B(xor_4_out), .C_in(Bit_toplama_5_c_out), .Sum(res[4]), .C_out(Bit_toplama_4_c_out));
  FullAdder_1b Bit_toplama_5 (
    .A(A[3]), .B(xor_5_out), .C_in(Bit_toplama_6_c_out), .Sum(res[3]), .C_out(Bit_toplama_5_c_out));
  FullAdder_1b Bit_toplama_6 (
    .A(A[2]), .B(xor_6_out), .C_in(Bit_toplama_7_c_out), .Sum(res[2]), .C_out(Bit_toplama_6_c_out));
  FullAdder_1b Bit_toplama_7 (
    .A(A[1]), .B(xor_7_out), .C_in(Bit_toplama_8_c_out), .Sum(res[1]), .C_out(Bit_toplama_7_c_out));
  FullAdder_1b Bit_toplama_8 (.A(A[0]), .B(xor_8_out), .C_in(Subtraction), .Sum(res[0]), .C_out(Bit_toplama_8_c_out));
endmodule
