// Logisim project Control_Unit.circ as structural Verilog: 1 circuit, main circuit Control_Unit
module Control_Unit (
  input  CLK,
  input  RESET,
  input  [3:0] OPCODE,
  output PC_OUT,
  output LI,
  output PC_INC,
  output EI,
  output L_MBR,
  output RI,
  output LM,
  output ALU_OUT,
  output LB,
  output LA,
  output LO,
  output A_OUT,
  output RO
);

  wire and_1_out, and_2_out, and_5_out, decoder_1_out1, decoder_1_out2, decoder_1_out14, decoder_1_out15,
       j_k_ff_1_q, j_k_ff_1_qn, j_k_ff_2_q, j_k_ff_2_qn, j_k_ff_3_q, j_k_ff_3_qn, or_4_out, T3_out, T4_out,
       T5_out;

  Decoder #(.enable("false"), .select(4)) decoder_1 (
    .out1(decoder_1_out1), .out2(decoder_1_out2), .out14(decoder_1_out14), .out15(decoder_1_out15),
    .sel(OPCODE));  // open: out0, out3, out4, out5, out6, out7, out8, out9, out10, out11, out12, out13
  and T0 (PC_OUT, j_k_ff_1_qn, j_k_ff_2_qn, j_k_ff_3_qn);
  or or_1 (LM, PC_OUT, EI);
  // AND_Gate T7 has open pins: in0=j_k_ff_1_qn, in1=j_k_ff_2_qn, in2=j_k_ff_3_q, out=open
  J_K_Flip_Flop #(.trigger("falling")) j_k_ff_1 (
    .J(1'b1), .K(1'b1), .clk(j_k_ff_2_qn), .Q(j_k_ff_1_q), .Qn(j_k_ff_1_qn), .preset(1'b0), .reset(RESET));
  J_K_Flip_Flop #(.trigger("falling")) j_k_ff_2 (
    .J(1'b1), .K(1'b1), .clk(j_k_ff_3_qn), .Q(j_k_ff_2_q), .Qn(j_k_ff_2_qn), .preset(1'b0), .reset(RESET));
  // AND_Gate T6 has open pins: in0=j_k_ff_1_qn, in1=j_k_ff_2_q, in2=j_k_ff_3_qn, out=open
  or or_2 (EI, and_1_out, and_2_out);
  and and_1 (and_1_out, T3_out, decoder_1_out1);
  and and_2 (and_2_out, T3_out, decoder_1_out2);
  and T5 (T5_out, j_k_ff_1_qn, j_k_ff_2_q, j_k_ff_3_q);
  and and_3 (ALU_OUT, T5_out, decoder_1_out1);
  and and_4 (A_OUT, decoder_1_out14, T3_out);
  J_K_Flip_Flop #(.trigger("falling")) j_k_ff_3 (
    .J(1'b1), .K(1'b1), .clk(CLK), .Q(j_k_ff_3_q), .Qn(j_k_ff_3_qn), .preset(1'b0), .reset(RESET));
  and T4 (T4_out, j_k_ff_1_q, j_k_ff_2_qn, j_k_ff_3_qn);
  and and_5 (and_5_out, T4_out, decoder_1_out2);
  and T3 (T3_out, j_k_ff_1_q, j_k_ff_2_qn, j_k_ff_3_q);
  and and_6 (LB, T4_out, decoder_1_out1);
  or or_3 (LA, ALU_OUT, and_5_out);
  or or_4 (or_4_out, and_5_out, LI);
  or or_5 (RO, LB, or_4_out);
  and T2 (LI, j_k_ff_1_q, j_k_ff_2_q, j_k_ff_3_qn);
  and T1 (PC_INC, j_k_ff_1_q, j_k_ff_2_q, j_k_ff_3_q);

  assign L_MBR = 1'b0;
  assign LO = A_OUT;
  assign RI = 1'b0;

  // Notes on the sheet:
  //   ADD
  //   LDA
  //   OUT
  //   HLT
endmodule
