// Logisim project Prog_Counter.circ as structural Verilog: 4 circuits, main circuit Program_Counter
module FullAdder_1b (
  input  A,
  input  B,
  input  C_in,
  output Sum,
  output C_out
);

  wire and_1_out, and_2_out, xor_1_out;

  and and_1 (and_1_out, A, B);
  xor xor_1 (xor_1_out, A, B);
  and and_2 (and_2_out, xor_1_out, C_in);
  xor xor_2 (Sum, xor_1_out, C_in);
  or or_1 (C_out, and_2_out, and_1_out);
endmodule

module ALU (
  input  [7:0] A,
  input  Subtraction,
  input  [7:0] B,
  output [7:0] res,
  output Overflow
);

  wire Bit_toplama_2_c_out, Bit_toplama_3_c_out, Bit_toplama_4_c_out, Bit_toplama_5_c_out,
       Bit_toplama_6_c_out, Bit_toplama_7_c_out, Bit_toplama_8_c_out, xor_1_out, xor_2_out, xor_3_out,
       xor_4_out, xor_5_out, xor_6_out, xor_7_out, xor_8_out;

  FullAdder_1b Bit_toplama_1 (.A(A[7]), .B(xor_1_out), .C_in(Bit_toplama_2_c_out), .Sum(res[7]), .C_out(Overflow));
  xor xor_1 (xor_1_out, B[7], Subtraction);
  xor xor_2 (xor_2_out, B[6], Subtraction);
  xor xor_3 (xor_3_out, B[5], Subtraction);
  xor xor_4 (xor_4_out, B[4], Subtraction);
  xor xor_5 (xor_5_out, B[3], Subtraction);
  xor xor_6 (xor_6_out, B[2], Subtraction);
  xor xor_7 (xor_7_out, B[1], Subtraction);
  xor xor_8 (xor_8_out, B[0], Subtraction);
  FullAdder_1b Bit_toplama_2 (
    .A(A[6]), .B(xor_2_out), .C_in(Bit_toplama_3_c_out), .Sum(res[6]), .C_out(Bit_toplama_2_c_out));
  FullAdder_1b Bit_toplama_3 (
    .A(A[5]), .B(xor_3_out), .C_in(Bit_toplama_4_c_out), .Sum(res[5]), .C_out(Bit_toplama_3_c_out));
  FullAdder_1b Bit_toplama_4 (
    .A(A[4]), .B(xor_4_out), .C_in(Bit_toplama_5_c_out), .Sum(res[4]), .C_out(Bit_toplama_4_c_out));
  FullAdder_1b Bit_toplama_5 (
    .A(A[3]), .B(xor_5_out), .C_in(Bit_toplama_6_c_out), .Sum(res[3]), .C_out(Bit_toplama_5_c_out));
  FullAdder_1b Bit_toplama_6 (
    .A(A[2]), .B(xor_6_out), .C_in(Bit_toplama_7_c_out), .Sum(res[2]), .C_out(Bit_toplama_6_c_out));
  FullAdder_1b Bit_toplama_7 (
    .A(A[1]), .B(xor_7_out), .C_in(Bit_toplama_8_c_out), .Sum(res[1]), .C_out(Bit_toplama_7_c_out));
  FullAdder_1b Bit_toplama_8 (.A(A[0]), .B(xor_8_out), .C_in(Subtraction), .Sum(res[0]), .C_out(Bit_toplama_8_c_out));
endmodule

module Register_8Bit (
  input  [7:0] Data_In,
  input  CLK,
  input  RESET,
  input  REG_OUT,
  output [7:0] Bus_Out,
  output [7:0] MONITOR
);

  D_Flip_Flop #(.trigger("falling")) d_ff_1 (
    .D(Data_In[0]), .clk(CLK), .Q(MONITOR[0]), .reset(RESET));  // open: Qn, preset
  D_Flip_Flop #(.trigger("falling")) d_ff_2 (
    .D(Data_In[1]), .clk(CLK), .Q(MONITOR[1]), .reset(RESET));  // open: Qn, preset
  D_Flip_Flop #(.trigger("falling")) d_ff_3 (
    .D(Data_In[2]), .clk(CLK), .Q(MONITOR[2]), .reset(RESET));  // open: Qn, preset
  D_Flip_Flop #(.trigger("falling")) d_ff_4 (
    .D(Data_In[3]), .clk(CLK), .Q(MONITOR[3]), .reset(RESET));  // open: Qn, preset
  D_Flip_Flop #(.trigger("falling")) d_ff_5 (
    .D(Data_In[4]), .clk(CLK), .Q(MONITOR[4]), .reset(RESET));  // open: Qn, preset
  D_Flip_Flop #(.trigger("falling")) d_ff_6 (
    .D(Data_In[5]), .clk(CLK), .Q(MONITOR[5]), .reset(RESET));  // open: Qn, preset
  D_Flip_Flop #(.trigger("falling")) d_ff_7 (
    .D(Data_In[6]), .clk(CLK), .Q(MONITOR[6]), .reset(RESET));  // open: Qn, preset
  D_Flip_Flop #(.trigger("falling")) d_ff_8 (
    .D(Data_In[7]), .clk(CLK), .Q(MONITOR[7]), .reset(RESET));  // open: Qn, preset
  assign Bus_Out[0] = REG_OUT ? MONITOR[0] : 1'bz;  // Controlled_Buffer controlled_buffer_1
  assign Bus_Out[1] = REG_OUT ? MONITOR[1] : 1'bz;  // Controlled_Buffer controlled_buffer_2
  assign Bus_Out[2] = REG_OUT ? MONITOR[2] : 1'bz;  // Controlled_Buffer controlled_buffer_3
  assign Bus_Out[3] = REG_OUT ? MONITOR[3] : 1'bz;  // Controlled_Buffer controlled_buffer_4
  assign Bus_Out[4] = REG_OUT ? MONITOR[4] : 1'bz;  // Controlled_Buffer controlled_buffer_5
  assign Bus_Out[5] = REG_OUT ? MONITOR[5] : 1'bz;  // Controlled_Buffer controlled_buffer_6
  assign Bus_Out[6] = REG_OUT ? MONITOR[6] : 1'bz;  // Controlled_Buffer controlled_buffer_7
  assign Bus_Out[7] = REG_OUT ? MONITOR[7] : 1'bz;  // Controlled_Buffer controlled_buffer_8
endmodule

module Program_Counter (
  input  CLK,
  input  PC_INC,
  input  RESET,
  input  PC_OUT,
  output [7:0] Output_bus_1
);

  wire and_1_out;
  wire [7:0] ALU_1_res, Register_8Bit_1_monitor;

  and and_1 (and_1_out, CLK, PC_INC);
  Register_8Bit Register_8Bit_1 (
    .Data_In(ALU_1_res), .CLK(and_1_out), .RESET(RESET), .REG_OUT(PC_OUT), .Bus_Out(Output_bus_1),
    .MONITOR(Register_8Bit_1_monitor));
  ALU ALU_1 (.A(Register_8Bit_1_monitor), .Subtraction(1'b0), .B(8'h1), .res(ALU_1_res));  // open: Overflow
endmodule
