// Logisim project Register_Unit.circ as structural Verilog: 1 circuit, main circuit Register_8Bit
module Register_8Bit (
  input  [7:0] Data_In,
  input  CLK,
  input  RESET,
  input  REG_OUT,
  output [7:0] Bus_Out,
  output [7:0] MONITOR
);

  D_Flip_Flop #(.trigger("falling")) d_ff_1 (
    .D(Data_In[0]), .clk(CLK), .Q(MONITOR[0]), .reset(RESET));  // open: Qn, preset
  D_Flip_Flop #(.trigger("falling")) d_ff_2 (
    .D(Data_In[1]), .clk(CLK), .Q(MONITOR[1]), .reset(RESET));  // open: Qn, preset
  D_Flip_Flop #(.trigger("falling")) d_ff_3 (
    .D(Data_In[2]), .clk(CLK), .Q(MONITOR[2]), .reset(RESET));  // open: Qn, preset
  D_Flip_Flop #(.trigger("falling")) d_ff_4 (
    .D(Data_In[3]), .clk(CLK), .Q(MONITOR[3]), .reset(RESET));  // open: Qn, preset
  D_Flip_Flop #(.trigger("falling")) d_ff_5 (
    .D(Data_In[4]), .clk(CLK), .Q(MONITOR[4]), .reset(RESET));  // open: Qn, preset
  D_Flip_Flop #(.trigger("falling")) d_ff_6 (
    .D(Data_In[5]), .clk(CLK), .Q(MONITOR[5]), .reset(RESET));  // open: Qn, preset
  D_Flip_Flop #(.trigger("falling")) d_ff_7 (
    .D(Data_In[6]), .clk(CLK), .Q(MONITOR[6]), .reset(RESET));  // open: Qn, preset
  D_Flip_Flop #(.trigger("falling")) d_ff_8 (
    .D(Data_In[7]), .clk(CLK), .Q(MONITOR[7]), .reset(RESET));  // open: Qn, preset
  assign Bus_Out[0] = REG_OUT ? MONITOR[0] : 1'bz;  // Controlled_Buffer controlled_buffer_1
  assign Bus_Out[1] = REG_OUT ? MONITOR[1] : 1'bz;  // Controlled_Buffer controlled_buffer_2
  assign Bus_Out[2] = REG_OUT ? MONITOR[2] : 1'bz;  // Controlled_Buffer controlled_buffer_3
  assign Bus_Out[3] = REG_OUT ? MONITOR[3] : 1'bz;  // Controlled_Buffer controlled_buffer_4
  assign Bus_Out[4] = REG_OUT ? MONITOR[4] : 1'bz;  // Controlled_Buffer controlled_buffer_5
  assign Bus_Out[5] = REG_OUT ? MONITOR[5] : 1'bz;  // Controlled_Buffer controlled_buffer_6
  assign Bus_Out[6] = REG_OUT ? MONITOR[6] : 1'bz;  // Controlled_Buffer controlled_buffer_7
  assign Bus_Out[7] = REG_OUT ? MONITOR[7] : 1'bz;  // Controlled_Buffer controlled_buffer_8
endmodule
