// Logisim project SRAM_4B.circ as structural Verilog: 2 circuits, main circuit RAM_4Byte
module Register_8Bit (
  input  [7:0] Data_In,
  input  CLK,
  input  RESET,
  input  REG_OUT,
  output [7:0] Bus_Out,
  output [7:0] MONITOR
);

  D_Flip_Flop #(.trigger("falling")) d_ff_1 (
    .D(Data_In[0]), .clk(CLK), .Q(MONITOR[0]), .reset(RESET));  // open: Qn, preset
  D_Flip_Flop #(.trigger("falling")) d_ff_2 (
    .D(Data_In[1]), .clk(CLK), .Q(MONITOR[1]), .reset(RESET));  // open: Qn, preset
  D_Flip_Flop #(.trigger("falling")) d_ff_3 (
    .D(Data_In[2]), .clk(CLK), .Q(MONITOR[2]), .reset(RESET));  // open: Qn, preset
  D_Flip_Flop #(.trigger("falling")) d_ff_4 (
    .D(Data_In[3]), .clk(CLK), .Q(MONITOR[3]), .reset(RESET));  // open: Qn, preset
  D_Flip_Flop #(.trigger("falling")) d_ff_5 (
    .D(Data_In[4]), .clk(CLK), .Q(MONITOR[4]), .reset(RESET));  // open: Qn, preset
  D_Flip_Flop #(.trigger("falling")) d_ff_6 (
    .D(Data_In[5]), .clk(CLK), .Q(MONITOR[5]), .reset(RESET));  // open: Qn, preset
  D_Flip_Flop #(.trigger("falling")) d_ff_7 (
    .D(Data_In[6]), .clk(CLK), .Q(MONITOR[6]), .reset(RESET));  // open: Qn, preset
  D_Flip_Flop #(.trigger("falling")) d_ff_8 (
    .D(Data_In[7]), .clk(CLK), .Q(MONITOR[7]), .reset(RESET));  // open: Qn, preset
  assign Bus_Out[0] = REG_OUT ? MONITOR[0] : 1'bz;  // Controlled_Buffer controlled_buffer_1
  assign Bus_Out[1] = REG_OUT ? MONITOR[1] : 1'bz;  // Controlled_Buffer controlled_buffer_2
  assign Bus_Out[2] = REG_OUT ? MONITOR[2] : 1'bz;  // Controlled_Buffer controlled_buffer_3
  assign Bus_Out[3] = REG_OUT ? MONITOR[3] : 1'bz;  // Controlled_Buffer controlled_buffer_4
  assign Bus_Out[4] = REG_OUT ? MONITOR[4] : 1'bz;  // Controlled_Buffer controlled_buffer_5
  assign Bus_Out[5] = REG_OUT ? MONITOR[5] : 1'bz;  // Controlled_Buffer controlled_buffer_6
  assign Bus_Out[6] = REG_OUT ? MONITOR[6] : 1'bz;  // Controlled_Buffer controlled_buffer_7
  assign Bus_Out[7] = REG_OUT ? MONITOR[7] : 1'bz;  // Controlled_Buffer controlled_buffer_8
endmodule

module RAM_4Byte (
  input  RI,
  input  [1:0] Address,
  input  RO,
  input  CLK,
  input  RESET,
  input  [7:0] DATA_IN,
  output [7:0] DATA_OUT
);

  wire and_1_out, and_2_out, and_3_out, and_4_out, decoder_1_out0, decoder_1_out1, decoder_1_out2,
       decoder_1_out3;
  wire [7:0] Address_0_bus_out;

  Decoder #(.enable("false"), .select(2)) decoder_1 (
    .out0(decoder_1_out0), .out1(decoder_1_out1), .out2(decoder_1_out2), .out3(decoder_1_out3), .sel(Address));
  and and_1 (and_1_out, RI, decoder_1_out0, CLK);
  and and_2 (and_2_out, RI, decoder_1_out1, CLK);
  and and_3 (and_3_out, RI, decoder_1_out2, CLK);
  and and_4 (and_4_out, RI, decoder_1_out3, CLK);
  Register_8Bit Address_0 (
    .Data_In(DATA_IN), .CLK(and_1_out), .RESET(RESET), .REG_OUT(decoder_1_out0), .Bus_Out(Address_0_bus_out));  // open: MONITOR
  Register_8Bit Address_1 (
    .Data_In(DATA_IN), .CLK(and_2_out), .RESET(RESET), .REG_OUT(decoder_1_out1), .Bus_Out(Address_0_bus_out));  // open: MONITOR
  Register_8Bit Address_2 (
    .Data_In(DATA_IN), .CLK(and_3_out), .RESET(RESET), .REG_OUT(decoder_1_out2), .Bus_Out(Address_0_bus_out));  // open: MONITOR
  Register_8Bit Address_3 (
    .Data_In(DATA_IN), .CLK(and_4_out), .RESET(RESET), .REG_OUT(decoder_1_out3), .Bus_Out(Address_0_bus_out));  // open: MONITOR
  assign DATA_OUT = RO ? Address_0_bus_out : 8'bz;  // Controlled_Buffer controlled_buffer_1
endmodule
