// Logisim project Top_Module.circ as structural Verilog: 9 circuits, main circuit MAIN_CPU
module FullAdder_1b (
  input  A,
  input  B,
  input  C_in,
  output Sum,
  output C_out
);

  wire and_1_out, and_2_out, xor_1_out;

  and and_1 (and_1_out, A, B);
  xor xor_1 (xor_1_out, A, B);
  and and_2 (and_2_out, xor_1_out, C_in);
  xor xor_2 (Sum, xor_1_out, C_in);
  or or_1 (C_out, and_2_out, and_1_out);
endmodule

module ALU (
  input  [7:0] A,
  input  Subtraction,
  input  [7:0] B,
  output [7:0] res,
  output Overflow
);

  wire Bit_toplama_2_c_out, Bit_toplama_3_c_out, Bit_toplama_4_c_out, Bit_toplama_5_c_out,
       Bit_toplama_6_c_out, Bit_toplama_7_c_out, Bit_toplama_8_c_out, xor_1_out, xor_2_out, xor_3_out,
       xor_4_out, xor_5_out, xor_6_out, xor_7_out, xor_8_out;

  FullAdder_1b Bit_toplama_1 (.A(A[7]), .B(xor_1_out), .C_in(Bit_toplama_2_c_out), .Sum(res[7]), .C_out(Overflow));
  xor xor_1 (xor_1_out, B[7], Subtraction);
  xor xor_2 (xor_2_out, B[6], Subtraction);
  xor xor_3 (xor_3_out, B[5], Subtraction);
  xor xor_4 (xor_4_out, B[4], Subtraction);
  xor xor_5 (xor_5_out, B[3], Subtraction);
  xor xor_6 (xor_6_out, B[2], Subtraction);
  xor xor_7 (xor_7_out, B[1], Subtraction);
  xor xor_8 (xor_8_out, B[0], Subtraction);
  FullAdder_1b Bit_toplama_2 (
    .A(A[6]), .B(xor_2_out), .C_in(Bit_toplama_3_c_out), .Sum(res[6]), .C_out(Bit_toplama_2_c_out));
  FullAdder_1b Bit_toplama_3 (
    .A(A[5]), .B(xor_3_out), .C_in(Bit_toplama_4_c_out), .Sum(res[5]), .C_out(Bit_toplama_3_c_out));
  FullAdder_1b Bit_toplama_4 (
    .A(A[4]), .B(xor_4_out), .C_in(Bit_toplama_5_c_out), .Sum(res[4]), .C_out(Bit_toplama_4_c_out));
  FullAdder_1b Bit_toplama_5 (
    .A(A[3]), .B(xor_5_out), .C_in(Bit_toplama_6_c_out), .Sum(res[3]), .C_out(Bit_toplama_5_c_out));
  FullAdder_1b Bit_toplama_6 (
    .A(A[2]), .B(xor_6_out), .C_in(Bit_toplama_7_c_out), .Sum(res[2]), .C_out(Bit_toplama_6_c_out));
  FullAdder_1b Bit_toplama_7 (
    .A(A[1]), .B(xor_7_out), .C_in(Bit_toplama_8_c_out), .Sum(res[1]), .C_out(Bit_toplama_7_c_out));
  FullAdder_1b Bit_toplama_8 (.A(A[0]), .B(xor_8_out), .C_in(Subtraction), .Sum(res[0]), .C_out(Bit_toplama_8_c_out));
endmodule

module Register_8Bit (
  input  [7:0] Data_In,
  input  CLK,
  input  RESET,
  input  REG_OUT,
  output [7:0] Bus_Out,
  output [7:0] MONITOR
);

  D_Flip_Flop #(.trigger("falling")) d_ff_1 (
    .D(Data_In[0]), .clk(CLK), .Q(MONITOR[0]), .reset(RESET));  // open: Qn, preset
  D_Flip_Flop #(.trigger("falling")) d_ff_2 (
    .D(Data_In[1]), .clk(CLK), .Q(MONITOR[1]), .reset(RESET));  // open: Qn, preset
  D_Flip_Flop #(.trigger("falling")) d_ff_3 (
    .D(Data_In[2]), .clk(CLK), .Q(MONITOR[2]), .reset(RESET));  // open: Qn, preset
  D_Flip_Flop #(.trigger("falling")) d_ff_4 (
    .D(Data_In[3]), .clk(CLK), .Q(MONITOR[3]), .reset(RESET));  // open: Qn, preset
  D_Flip_Flop #(.trigger("falling")) d_ff_5 (
    .D(Data_In[4]), .clk(CLK), .Q(MONITOR[4]), .reset(RESET));  // open: Qn, preset
  D_Flip_Flop #(.trigger("falling")) d_ff_6 (
    .D(Data_In[5]), .clk(CLK), .Q(MONITOR[5]), .reset(RESET));  // open: Qn, preset
  D_Flip_Flop #(.trigger("falling")) d_ff_7 (
    .D(Data_In[6]), .clk(CLK), .Q(MONITOR[6]), .reset(RESET));  // open: Qn, preset
  D_Flip_Flop #(.trigger("falling")) d_ff_8 (
    .D(Data_In[7]), .clk(CLK), .Q(MONITOR[7]), .reset(RESET));  // open: Qn, preset
  assign Bus_Out[0] = REG_OUT ? MONITOR[0] : 1'bz;  // Controlled_Buffer controlled_buffer_1
  assign Bus_Out[1] = REG_OUT ? MONITOR[1] : 1'bz;  // Controlled_Buffer controlled_buffer_2
  assign Bus_Out[2] = REG_OUT ? MONITOR[2] : 1'bz;  // Controlled_Buffer controlled_buffer_3
  assign Bus_Out[3] = REG_OUT ? MONITOR[3] : 1'bz;  // Controlled_Buffer controlled_buffer_4
  assign Bus_Out[4] = REG_OUT ? MONITOR[4] : 1'bz;  // Controlled_Buffer controlled_buffer_5
  assign Bus_Out[5] = REG_OUT ? MONITOR[5] : 1'bz;  // Controlled_Buffer controlled_buffer_6
  assign Bus_Out[6] = REG_OUT ? MONITOR[6] : 1'bz;  // Controlled_Buffer controlled_buffer_7
  assign Bus_Out[7] = REG_OUT ? MONITOR[7] : 1'bz;  // Controlled_Buffer controlled_buffer_8
endmodule

module MAIN_CPU (
  input  MANUEL_DATA_OE,
  input  [7:0] MANUEL_DATA,
  input  Sub,
  input  B_OUT,
  input  LM,
  input  PROG_MODE,
  input  L_MBR,
  input  RI
);

  wire and_1_out, and_2_out, and_3_out, and_4_out, and_5_out, and_6_out, and_7_out, and_8_out, and_9_out,
       Control_Unit_1_a_out, Control_Unit_1_alu_out, Control_Unit_1_ei, Control_Unit_1_l_mbr,
       Control_Unit_1_la, Control_Unit_1_lb, Control_Unit_1_li, Control_Unit_1_lm, Control_Unit_1_lo,
       Control_Unit_1_pc_inc, Control_Unit_1_pc_out, Control_Unit_1_ri, Control_Unit_1_ro, MAIN_CLK_out,
       MAIN_RESET_out, not_1_out, or_1_out, or_2_out, or_3_out;
  wire [7:0] ALU_1_res, IR_1_monitor, MAR_monitor, MBR_monitor, OUT_REG_monitor,
       Program_Counter_1_output_bus_1, Register_A_monitor, Register_B_monitor;

  Button MAIN_CLK (.out(MAIN_CLK_out));
  Button MAIN_RESET (.out(MAIN_RESET_out));
  and and_1 (and_1_out, Control_Unit_1_lb, MAIN_CLK_out);
  and and_2 (and_2_out, MAIN_CLK_out, not_1_out);
  not not_1 (not_1_out, PROG_MODE);
  and and_3 (and_3_out, MAIN_CLK_out, Control_Unit_1_li);
  and and_4 (and_4_out, MAIN_CLK_out, Control_Unit_1_la);
  and and_5 (and_5_out, not_1_out, Control_Unit_1_pc_out);
  Program_Counter Program_Counter_1 (
    .CLK(MAIN_CLK_out), .PC_INC(Control_Unit_1_pc_inc), .RESET(MAIN_RESET_out), .PC_OUT(and_5_out),
    .Output_bus_1(Program_Counter_1_output_bus_1));
  IR IR_1 (
    .Data_In(Program_Counter_1_output_bus_1), .CLK(and_3_out), .RESET(MAIN_RESET_out), .MONITOR(IR_1_monitor));  // open: ENABLE, Bus_Out
  Register_8Bit Register_A (
    .Data_In(Program_Counter_1_output_bus_1), .CLK(and_4_out), .RESET(MAIN_RESET_out),
    .REG_OUT(Control_Unit_1_a_out), .Bus_Out(Program_Counter_1_output_bus_1), .MONITOR(Register_A_monitor));
  ALU ALU_1 (.A(Register_A_monitor), .Subtraction(Sub), .B(Register_B_monitor), .res(ALU_1_res));  // open: Overflow
  Register_8Bit Register_B (
    .Data_In(Program_Counter_1_output_bus_1), .CLK(and_1_out), .RESET(MAIN_RESET_out), .REG_OUT(B_OUT),
    .Bus_Out(Program_Counter_1_output_bus_1), .MONITOR(Register_B_monitor));
  Control_Unit Control_Unit_1 (
    .CLK(and_2_out), .RESET(MAIN_RESET_out), .OPCODE(IR_1_monitor[7:4]), .PC_OUT(Control_Unit_1_pc_out),
    .LI(Control_Unit_1_li), .PC_INC(Control_Unit_1_pc_inc), .EI(Control_Unit_1_ei),
    .L_MBR(Control_Unit_1_l_mbr), .RI(Control_Unit_1_ri), .LM(Control_Unit_1_lm),
    .ALU_OUT(Control_Unit_1_alu_out), .LB(Control_Unit_1_lb), .LA(Control_Unit_1_la), .LO(Control_Unit_1_lo),
    .A_OUT(Control_Unit_1_a_out), .RO(Control_Unit_1_ro));
  assign Program_Counter_1_output_bus_1 = Control_Unit_1_alu_out ? ALU_1_res : 8'bz;  // Controlled_Buffer controlled_buffer_1
  assign Program_Counter_1_output_bus_1 = Control_Unit_1_ei ? {4'b0000, IR_1_monitor[3:0]} : 8'bz;  // Controlled_Buffer controlled_buffer_2
  and and_6 (and_6_out, not_1_out, Control_Unit_1_lm);
  or or_1 (or_1_out, Control_Unit_1_ri, RI);
  or or_2 (or_2_out, and_6_out, LM);
  and and_7 (and_7_out, MAIN_CLK_out, or_2_out);
  or or_3 (or_3_out, L_MBR, Control_Unit_1_l_mbr);
  and and_8 (and_8_out, MAIN_CLK_out, or_3_out);
  and and_9 (and_9_out, MAIN_CLK_out, Control_Unit_1_lo);
  Register_8Bit MAR (
    .Data_In(Program_Counter_1_output_bus_1), .CLK(and_7_out), .RESET(MAIN_RESET_out), .MONITOR(MAR_monitor));  // open: REG_OUT, Bus_Out
  Register_8Bit MBR (
    .Data_In(Program_Counter_1_output_bus_1), .CLK(and_8_out), .MONITOR(MBR_monitor));  // open: RESET, REG_OUT, Bus_Out
  Register_8Bit OUT_REG (
    .Data_In(Program_Counter_1_output_bus_1), .CLK(and_9_out), .RESET(MAIN_RESET_out), .REG_OUT(1'b0),
    .MONITOR(OUT_REG_monitor));  // open: Bus_Out
  Hex_Digit_Display Hex_Digit_Display_1 (.value(OUT_REG_monitor[7:4]));  // open: dp
  Hex_Digit_Display Hex_Digit_Display_2 (.value(OUT_REG_monitor[3:0]));  // open: dp
  RAM_16Byte RAM_16Byte_1 (
    .DATA_IN(MBR_monitor), .CLK(MAIN_CLK_out), .RI(or_1_out), .RO(Control_Unit_1_ro), .ADRES(MAR_monitor),
    .DATA_OUT(Program_Counter_1_output_bus_1));
  assign Program_Counter_1_output_bus_1 = MANUEL_DATA_OE ? MANUEL_DATA : 8'bz;  // Controlled_Buffer controlled_buffer_3

  // Notes on the sheet:
  //   LB
  //   CLK
  //   CLK
  //   LI
  //   CLK
  //   LA
  //   OPCODE
  //   ALU_OUT
  //   MAİN BUS
  //   EI
  //   LM
  //   CLK
  //   LO
  //   Hexadecimal
  //   Hexadecimal
endmodule

module Control_Unit (
  input  CLK,
  input  RESET,
  input  [3:0] OPCODE,
  output PC_OUT,
  output LI,
  output PC_INC,
  output EI,
  output L_MBR,
  output RI,
  output LM,
  output ALU_OUT,
  output LB,
  output LA,
  output LO,
  output A_OUT,
  output RO
);

  wire and_1_out, and_2_out, and_5_out, decoder_1_out1, decoder_1_out2, decoder_1_out14, decoder_1_out15,
       j_k_ff_1_q, j_k_ff_1_qn, j_k_ff_2_q, j_k_ff_2_qn, j_k_ff_3_q, j_k_ff_3_qn, or_4_out, T3_out, T4_out,
       T5_out;

  Decoder #(.enable("false"), .select(4)) decoder_1 (
    .out1(decoder_1_out1), .out2(decoder_1_out2), .out14(decoder_1_out14), .out15(decoder_1_out15),
    .sel(OPCODE));  // open: out0, out3, out4, out5, out6, out7, out8, out9, out10, out11, out12, out13
  and T0 (PC_OUT, j_k_ff_1_qn, j_k_ff_2_qn, j_k_ff_3_qn);
  or or_1 (LM, PC_OUT, EI);
  // AND_Gate T7 has open pins: in0=j_k_ff_1_qn, in1=j_k_ff_2_qn, in2=j_k_ff_3_q, out=open
  J_K_Flip_Flop #(.trigger("falling")) j_k_ff_1 (
    .J(1'b1), .K(1'b1), .clk(j_k_ff_2_qn), .Q(j_k_ff_1_q), .Qn(j_k_ff_1_qn), .preset(1'b0), .reset(RESET));
  J_K_Flip_Flop #(.trigger("falling")) j_k_ff_2 (
    .J(1'b1), .K(1'b1), .clk(j_k_ff_3_qn), .Q(j_k_ff_2_q), .Qn(j_k_ff_2_qn), .preset(1'b0), .reset(RESET));
  // AND_Gate T6 has open pins: in0=j_k_ff_1_qn, in1=j_k_ff_2_q, in2=j_k_ff_3_qn, out=open
  or or_2 (EI, and_1_out, and_2_out);
  and and_1 (and_1_out, T3_out, decoder_1_out1);
  and and_2 (and_2_out, T3_out, decoder_1_out2);
  and T5 (T5_out, j_k_ff_1_qn, j_k_ff_2_q, j_k_ff_3_q);
  and and_3 (ALU_OUT, T5_out, decoder_1_out1);
  and and_4 (A_OUT, decoder_1_out14, T3_out);
  J_K_Flip_Flop #(.trigger("falling")) j_k_ff_3 (
    .J(1'b1), .K(1'b1), .clk(CLK), .Q(j_k_ff_3_q), .Qn(j_k_ff_3_qn), .preset(1'b0), .reset(RESET));
  and T4 (T4_out, j_k_ff_1_q, j_k_ff_2_qn, j_k_ff_3_qn);
  and and_5 (and_5_out, T4_out, decoder_1_out2);
  and T3 (T3_out, j_k_ff_1_q, j_k_ff_2_qn, j_k_ff_3_q);
  and and_6 (LB, T4_out, decoder_1_out1);
  or or_3 (LA, ALU_OUT, and_5_out);
  or or_4 (or_4_out, and_5_out, LI);
  or or_5 (RO, LB, or_4_out);
  and T2 (LI, j_k_ff_1_q, j_k_ff_2_q, j_k_ff_3_qn);
  and T1 (PC_INC, j_k_ff_1_q, j_k_ff_2_q, j_k_ff_3_q);

  assign L_MBR = 1'b0;
  assign LO = A_OUT;
  assign RI = 1'b0;

  // Notes on the sheet:
  //   ADD
  //   LDA
  //   OUT
  //   HLT
endmodule

module Program_Counter (
  input  CLK,
  input  PC_INC,
  input  RESET,
  input  PC_OUT,
  output [7:0] Output_bus_1
);

  wire and_1_out;
  wire [7:0] ALU_1_res, Register_8Bit_1_monitor;

  and and_1 (and_1_out, CLK, PC_INC);
  Register_8Bit Register_8Bit_1 (
    .Data_In(ALU_1_res), .CLK(and_1_out), .RESET(RESET), .REG_OUT(PC_OUT), .Bus_Out(Output_bus_1),
    .MONITOR(Register_8Bit_1_monitor));
  ALU ALU_1 (.A(Register_8Bit_1_monitor), .Subtraction(1'b0), .B(8'h1), .res(ALU_1_res));  // open: Overflow
endmodule

module RAM_4Byte (
  input  RI,
  input  [1:0] Address,
  input  RO,
  input  CLK,
  input  RESET,
  input  [7:0] DATA_IN,
  output [7:0] DATA_OUT
);

  wire and_1_out, and_2_out, and_3_out, and_4_out, decoder_1_out0, decoder_1_out1, decoder_1_out2,
       decoder_1_out3;
  wire [7:0] Address_0_bus_out;

  Decoder #(.enable("false"), .select(2)) decoder_1 (
    .out0(decoder_1_out0), .out1(decoder_1_out1), .out2(decoder_1_out2), .out3(decoder_1_out3), .sel(Address));
  and and_1 (and_1_out, RI, decoder_1_out0, CLK);
  and and_2 (and_2_out, RI, decoder_1_out1, CLK);
  and and_3 (and_3_out, RI, decoder_1_out2, CLK);
  and and_4 (and_4_out, RI, decoder_1_out3, CLK);
  Register_8Bit Address_0 (
    .Data_In(DATA_IN), .CLK(and_1_out), .RESET(RESET), .REG_OUT(decoder_1_out0), .Bus_Out(Address_0_bus_out));  // open: MONITOR
  Register_8Bit Address_1 (
    .Data_In(DATA_IN), .CLK(and_2_out), .RESET(RESET), .REG_OUT(decoder_1_out1), .Bus_Out(Address_0_bus_out));  // open: MONITOR
  Register_8Bit Address_2 (
    .Data_In(DATA_IN), .CLK(and_3_out), .RESET(RESET), .REG_OUT(decoder_1_out2), .Bus_Out(Address_0_bus_out));  // open: MONITOR
  Register_8Bit Address_3 (
    .Data_In(DATA_IN), .CLK(and_4_out), .RESET(RESET), .REG_OUT(decoder_1_out3), .Bus_Out(Address_0_bus_out));  // open: MONITOR
  assign DATA_OUT = RO ? Address_0_bus_out : 8'bz;  // Controlled_Buffer controlled_buffer_1
endmodule

module RAM_16Byte (
  input  [7:0] DATA_IN,
  input  CLK,
  input  RI,
  input  RO,
  input  [7:0] ADRES,
  output [7:0] DATA_OUT
);

  wire and_1_out, and_2_out, and_3_out, and_4_out, and_5_out, and_6_out, and_7_out, and_8_out,
       decoder_1_out0, decoder_1_out1, decoder_1_out2, decoder_1_out3;

  Decoder #(.enable("false"), .select(2)) decoder_1 (
    .out0(decoder_1_out0), .out1(decoder_1_out1), .out2(decoder_1_out2), .out3(decoder_1_out3),
    .sel(ADRES[3:2]));
  and and_1 (and_1_out, RI, decoder_1_out0);
  and and_2 (and_2_out, decoder_1_out0, RO);
  and and_3 (and_3_out, RI, decoder_1_out1);
  and and_4 (and_4_out, decoder_1_out1, RO);
  and and_5 (and_5_out, decoder_1_out2, RI);
  and and_6 (and_6_out, decoder_1_out2, RO);
  and and_7 (and_7_out, decoder_1_out3, RI);
  and and_8 (and_8_out, decoder_1_out3, RO);
  RAM_4Byte RAM_4Byte_1 (
    .RI(and_1_out), .Address(ADRES[1:0]), .RO(and_2_out), .CLK(CLK), .DATA_IN(DATA_IN), .DATA_OUT(DATA_OUT));  // open: RESET
  RAM_4Byte RAM_4Byte_2 (
    .RI(and_3_out), .Address(ADRES[1:0]), .RO(and_4_out), .CLK(CLK), .DATA_IN(DATA_IN), .DATA_OUT(DATA_OUT));  // open: RESET
  RAM_4Byte RAM_4Byte_3 (
    .RI(and_5_out), .Address(ADRES[1:0]), .RO(and_6_out), .CLK(CLK), .DATA_IN(DATA_IN), .DATA_OUT(DATA_OUT));  // open: RESET
  RAM_4Byte RAM_4Byte_4 (
    .RI(and_7_out), .Address(ADRES[1:0]), .RO(and_8_out), .CLK(CLK), .DATA_IN(DATA_IN), .DATA_OUT(DATA_OUT));  // open: RESET

  // Notes on the sheet:
  //   BANK 0
  //   BANK 1
  //   BANK 2
  //   BANK 3
endmodule

module IR (
  input  [7:0] Data_In,
  input  CLK,
  input  RESET,
  input  ENABLE,
  output [7:0] Bus_Out,
  output [7:0] MONITOR
);

  D_Flip_Flop #(.trigger("falling")) d_ff_1 (
    .D(Data_In[0]), .clk(CLK), .Q(MONITOR[0]), .reset(RESET));  // open: Qn, preset
  D_Flip_Flop #(.trigger("falling")) d_ff_2 (
    .D(Data_In[1]), .clk(CLK), .Q(MONITOR[1]), .reset(RESET));  // open: Qn, preset
  D_Flip_Flop #(.trigger("falling")) d_ff_3 (
    .D(Data_In[2]), .clk(CLK), .Q(MONITOR[2]), .reset(RESET));  // open: Qn, preset
  D_Flip_Flop #(.trigger("falling")) d_ff_4 (
    .D(Data_In[3]), .clk(CLK), .Q(MONITOR[3]), .reset(RESET));  // open: Qn, preset
  D_Flip_Flop #(.trigger("falling")) d_ff_5 (
    .D(Data_In[4]), .clk(CLK), .Q(MONITOR[4]), .reset(RESET));  // open: Qn, preset
  D_Flip_Flop #(.trigger("falling")) d_ff_6 (
    .D(Data_In[5]), .clk(CLK), .Q(MONITOR[5]), .reset(RESET));  // open: Qn, preset
  D_Flip_Flop #(.trigger("falling")) d_ff_7 (
    .D(Data_In[6]), .clk(CLK), .Q(MONITOR[6]), .reset(RESET));  // open: Qn, preset
  D_Flip_Flop #(.trigger("falling")) d_ff_8 (
    .D(Data_In[7]), .clk(CLK), .Q(MONITOR[7]), .reset(RESET));  // open: Qn, preset
  assign Bus_Out[0] = ENABLE ? MONITOR[0] : 1'bz;  // Controlled_Buffer controlled_buffer_1
  assign Bus_Out[1] = ENABLE ? MONITOR[1] : 1'bz;  // Controlled_Buffer controlled_buffer_2
  assign Bus_Out[2] = ENABLE ? MONITOR[2] : 1'bz;  // Controlled_Buffer controlled_buffer_3
  assign Bus_Out[3] = ENABLE ? MONITOR[3] : 1'bz;  // Controlled_Buffer controlled_buffer_4
  assign Bus_Out[4] = ENABLE ? MONITOR[4] : 1'bz;  // Controlled_Buffer controlled_buffer_5
  assign Bus_Out[5] = ENABLE ? MONITOR[5] : 1'bz;  // Controlled_Buffer controlled_buffer_6
  assign Bus_Out[6] = ENABLE ? MONITOR[6] : 1'bz;  // Controlled_Buffer controlled_buffer_7
  assign Bus_Out[7] = ENABLE ? MONITOR[7] : 1'bz;  // Controlled_Buffer controlled_buffer_8
endmodule
